# Fritzing sketch AZ_1.3 (saved by Fritzing 0.9.4)
breadboards: 1

parts:
  U1 = 74HC04_HEX_INVERTER [package=dil14]
  LED1 = smd LED [color="Red (633nm)" package="1206 [SMD]"]
  VCC1 = 4 x AAA Battery Mount

nets:
  N1: U1.1A, U1.VCC, VCC1.+
  N2: U1.1Y, U1.2A
  N3: U1.2Y, U1.3A
  N4: U1.3Y, U1.4A
  N5: U1.GND, LED1.cathode, VCC1.-
  N6: U1.4Y, U1.5A
  N7: U1.5Y, U1.6A
  N8: U1.6Y, LED1.anode
