// Logisim project AZ_2.2.circ as structural Verilog: 1 circuit, main circuit main
module main (
  input  C_in,
  input  in_2,
  input  a0,
  input  b1,
  input  a1,
  input  b2,
  input  a2,
  input  b3,
  input  a3,
  output c0,
  output c1,
  output c2,
  output c3,
  output Overflow_Detector,
  output C_out
);

  wire and_1_out, and_2_out, and_3_out, and_4_out, and_5_out, and_6_out, and_7_out, and_8_out, xor_1_out,
       xor_2_out, xor_3_out, xor_4_out, xor_5_out, xor_6_out, xor_7_out, xor_8_out, xor_9_out, xor_11_out,
       xor_12_out;

  xor xor_1 (xor_1_out, C_in, b1);
  xor xor_2 (xor_2_out, C_in, b2);
  xor xor_3 (xor_3_out, C_in, b3);
  xor xor_4 (xor_4_out, C_in, in_2);
  and and_1 (and_1_out, xor_4_out, a0);
  and and_2 (and_2_out, xor_1_out, a1);
  xor xor_5 (xor_5_out, xor_4_out, a0);
  xor xor_6 (xor_6_out, and_7_out, and_1_out);
  xor xor_7 (xor_7_out, xor_1_out, a1);
  xor xor_8 (xor_8_out, xor_2_out, a2);
  and and_3 (and_3_out, xor_2_out, a2);
  xor xor_9 (xor_9_out, xor_3_out, a3);
  and and_4 (and_4_out, xor_3_out, a3);
  xor xor_10 (c1, xor_6_out, xor_7_out);
  and and_5 (and_5_out, xor_6_out, xor_7_out);
  xor xor_11 (xor_11_out, and_5_out, and_2_out);
  xor xor_12 (xor_12_out, and_8_out, and_3_out);
  and and_6 (and_6_out, xor_12_out, xor_9_out);
  xor xor_13 (c0, C_in, xor_5_out);
  and and_7 (and_7_out, C_in, xor_5_out);
  xor xor_14 (c2, xor_11_out, xor_8_out);
  and and_8 (and_8_out, xor_11_out, xor_8_out);
  xor xor_15 (c3, xor_12_out, xor_9_out);
  xor xor_16 (C_out, and_6_out, and_4_out);
  xor xor_17 (Overflow_Detector, xor_12_out, C_out);
endmodule
